# Fritzing sketch Circuit Design - Server (saved by Fritzing 0.9.3b)
breadboards: 1

parts:
  U1 = ESP8266 NodeMCU LoLin module
  VCC2 = Battery block 9V
  KY-1 = Keyes Relay [package=THT]
  Amperemeter1 = Amperemeter

nets:
  N1: U1.3V3, KY-1.signal
  N2: U1.GND, VCC2.-, KY-1.power
  N3: U1.D5, KY-1.ground
  N4: U1.Vin, Amperemeter1.Positive

custom parts:
  ESP8266 NodeMCU LoLin module: ESP8266 based NodeMCU
  Keyes Relay: The Keyes 5V relay module is suitable for SCM development, home appliance control. It uses a 5V~12V TIL control signal which can control DC / AC signal.
  Amperemeter: A Standard Multimeter in Current mode
