# Fritzing sketch Circuit Design - Station (saved by Fritzing 0.9.3b)
breadboards: 1

parts:
  DHT1 = Humidity and Temperature Sensor DHT11
  U2 = ESP8266 NodeMCU LoLin module
  VCC1 = Battery block 9V
  Amperemeter1 = Amperemeter

nets:
  VCC: DHT1.Vcc, U2.3V3
  N1: DHT1.Data-signal, U2.D5
  N2: DHT1.GND_2, U2.GND, VCC1.-
  N3: U2.D0, U2.RST
  N4: U2.Vin, Amperemeter1.Positive

custom parts:
  Humidity and Temperature Sensor DHT11: Digital relative humidity & temperature sensor DHT11
  ESP8266 NodeMCU LoLin module: ESP8266 based NodeMCU
  Amperemeter: A Standard Multimeter in Current mode
