# Fritzing sketch Circuit Design (saved by Fritzing 0.9.3b)
breadboards: 2

parts:
  U1 = ESP8266 NodeMCU LoLin module
  DHT1 = Humidity and Temperature Sensor DHT11
  U2 = ESP8266 NodeMCU LoLin module
  VCC1 = Battery block 9V
  VCC2 = Battery block 9V
  KY-1 = Keyes Relay [package=THT]

nets:
  N1: U1.3V3, KY-1.signal
  N2: U1.GND, VCC2.-, KY-1.power
  N3: U1.D5, KY-1.ground
  N4: U1.Vin, VCC2.+
  VCC: DHT1.Vcc, U2.3V3
  N5: DHT1.Data-signal, U2.D5
  N6: DHT1.GND_2, U2.GND, VCC1.-
  N7: U2.D0, U2.RST
  N8: U2.Vin, VCC1.+

custom parts:
  ESP8266 NodeMCU LoLin module: ESP8266 based NodeMCU
  Humidity and Temperature Sensor DHT11: Digital relative humidity & temperature sensor DHT11
  Keyes Relay: The Keyes 5V relay module is suitable for SCM development, home appliance control. It uses a 5V~12V TIL control signal which can control DC / AC signal.
